# Fritzing sketch advanced (saved by Fritzing 0.9.6b)

parts:
  U1 = NodeMCU V1.0
  LED2 = LEDs [package=led10mm]
  Part2 = Lilypad Battery Connect
  M1 = ac light dimmer 3terminal
  U2 = Breadboard Power Supply [package=THT]

nets:
  N1: U1.D1, M1.PWM
  N2: U1.D2, M1.Z-C
  N3: U1.Vin, U2.pin8
  N4: U1.GND, U2.pin6
  N5: LED2.A, Part2.-, M1.N
  N6: LED2.C, M1.OUT
  N7: Part2.+, M1.IN
  N8: M1.VCC, U2.pin4
  N9: M1.GND, U2.pin2

notes:
  GND
  VCC 5V
  230V AC power supply
  VCC 3.3V

custom parts:
  NodeMCU V1.0: ESP9266 based NodeMCU
  LEDs: LEDs Standard schematic elements and footprints for 5mm, 3mm, 1206, and 0603 sized LEDs. 5mm - Spark Fun Electronics SKU : COM-00529 (and others)
  ac light dimmer 3terminal: ac light dimmer module 3 output terminals.
  Breadboard Power Supply: Représentation Carte Breadboard Power Supply
